# Fritzing sketch Stepper_ultra_keypad_infrared_LCD (saved by Fritzing 0.9.3b)
breadboards: 1

parts:
  Part1 = Arduino Uno (Rev3)
  IC1 = H-Bridge [package=THT]
  hc-sr1 = hc-sr04
  Matrix_keypad1 = KEYPAD 4x4
  LCM1602_IIC1 = LCM1602 IIC [part_number="LCM1602 IIC" chip_label="LCM1602 IIC" package="DIP (Dual Inline) [THT]"]
  LCD1 = LCD screen
  LED2 = LED - 5mm [color="Infrared (940nm)" package="5 mm [THT]"]
  LED3 = LED - 5mm [color="Infrared (940nm)" package="5 mm [THT]"]
  LED4 = LED - 5mm [color="Infrared (940nm)" package="5 mm [THT]"]
  LED5 = LED - 5mm [color="Infrared (850nm)" package="5 mm [THT]"]
  LED6 = LED - 5mm [color="Infrared (850nm)" package="5 mm [THT]"]
  LED7 = LED - 5mm [color="Infrared (850nm)" package="5 mm [THT]"]
  LED8 = LED - 5mm [color="Infrared (940nm)" package="5 mm [THT]"]
  LED9 = LED - 5mm [color="Infrared (850nm)" package="5 mm [THT]"]
  M1 = Stepper Motor - Bipolar
  R1 = Resistor [tolerance=±5% resistance=10k package=THT]
  R2 = Resistor [tolerance=±5% resistance=10k package=THT]
  R3 = Resistor [tolerance=±5% resistance=10k package=THT]
  R4 = Resistor [tolerance=±5% resistance=10k package=THT]
  R5 = Resistor [tolerance=±5% resistance=330 package=THT]
  R6 = Resistor [tolerance=±5% resistance=330 package=THT]
  R7 = Resistor [tolerance=±5% resistance=330 package=THT]
  R8 = Resistor [tolerance=±5% resistance=330 package=THT]
  J1 = Basic Servo

nets:
  N1: Part1.A4/SDA, LCM1602_IIC1.SDA
  N2: Part1.A5/SCL, LCM1602_IIC1.SCL
  N3: Part1.D8, Matrix_keypad1.row2
  N4: Part1.D9_PWM, Matrix_keypad1.row1
  N5: Part1.D10_PWM/SS, Matrix_keypad1.col4
  N6: Part1.D11_PWM/MOSI, Matrix_keypad1.col3
  N7: Part1.D12/MISO, Matrix_keypad1.col2
  N8: Part1.D13/SCK, Matrix_keypad1.col1
  N9: Part1.D0/RX, IC1.1A
  N10: Part1.D1/TX, Matrix_keypad1.row4
  N11: Part1.D2, hc-sr1.Trig
  N12: Part1.D3_PWM, hc-sr1.Echo
  N13: Part1.D4, IC1.3A
  N14: Part1.D5_PWM, IC1.4A
  N15: Part1.D6_PWM, IC1.2A
  N16: Part1.D7, Matrix_keypad1.row3
  N17: Part1.3V3, IC1.VCC2
  GND: Part1.GND, IC1.GND3, hc-sr1.GND, LCM1602_IIC1.GND, R6.Pin_0, R7.Pin_0, J1.gnd
  N18: IC1.2Y, M1.C
  N19: IC1.3Y, M1.B
  VCC: hc-sr1.VCC, LCM1602_IIC1.VCC, LED2.anode, LED3.anode, LED4.anode, LED8.anode, R1.Pin_0, R2.Pin_0, R3.Pin_0, R4.Pin_0
  VSS: LCM1602_IIC1.VSS, LCD1.VSS
  VDD: LCM1602_IIC1.VDD, LCD1.VDD
  N20: LCM1602_IIC1.V0, LCD1.V0
  N21: LCM1602_IIC1.RS, LCD1.RS
  N22: LCM1602_IIC1.RW, LCD1.R/W
  N23: LCM1602_IIC1.E, LCD1.E
  N24: LCM1602_IIC1.D0, LCD1.DB0
  N25: LCM1602_IIC1.D1, LCD1.DB1
  N26: LCM1602_IIC1.D2, LCD1.DB2
  N27: LCM1602_IIC1.D3, LCD1.DB3
  N28: LCM1602_IIC1.D4, LCD1.DB4
  N29: LCM1602_IIC1.D5, LCD1.DB5
  N30: LCM1602_IIC1.D6, LCD1.DB6
  N31: LCM1602_IIC1.D7, LCD1.DB7
  N32: LCM1602_IIC1.A, LCD1.LED+
  N33: LCM1602_IIC1.K, LCD1.LED-
  N34: LED5.anode, R5.Pin_1
  N35: LED6.anode, R8.Pin_1
  N36: LED7.anode, R6.Pin_1
  N37: LED9.anode, R7.Pin_1

custom parts:
  KEYPAD 4x4: Matrix keypad 16 buttons, 4 rows x 4 columns
  LCM1602 IIC: I2C-Module to use a 1602 or 2004 LCD on with the wire.h libory Serial LCD Modul

// code stored in the sketch: rep_stepper_ultra_keypad.ino
Stepper myStepper(stepsPerRevolution, 8, 9, 10, 11);

void setup() {
  myStepper.setSpeed(100);
  Serial.begin(9600);
}

void loop() {
  // 1 rotation clockwise: 
  Serial.println("clockwise");
  myStepper.step(stepsPerRevolution);
  delay(2000);

  // 1 rotation counterclockwise:
  Serial.println("counterclockwise");
  myStepper.step(-stepsPerRevolution);
  delay(2000);
}
